// Logisim project 8_BIT_ALU.circ as structural Verilog: 1 circuit, main circuit main
module main (
  input  [7:0] A,
  input  [7:0] B,
  input  [3:0] OPCODE,
  output V,
  output Ca,
  output Bo,
  output Z,
  output N,
  output [7:0] Y
);

  wire comparator_1_eq, xnor_1_out, xor_2_out;
  wire [7:0] adder_1_out, and_1_out, bit_extender_1_out, not_1_out, or_1_out, shifter_1_out, shifter_2_out,
       subtractor_1_out, xor_1_out;

  Adder adder_1 (.a(A), .b(B), .out(adder_1_out), .cout(Ca));  // open: cin
  Subtractor subtractor_1 (.a(A), .b(B), .out(subtractor_1_out), .bout(Bo));  // open: bin
  assign and_1_out = A & B;  // AND_Gate and_1, 8 bits wide
  assign or_1_out = A | B;  // OR_Gate or_1, 8 bits wide
  assign xor_1_out = A ^ B;  // XOR_Gate xor_1, 8 bits wide
  assign not_1_out = ~A;  // NOT_Gate not_1, 8 bits wide
  Shifter shifter_1 (.in(A), .\dist (B[2:0]), .out(shifter_1_out));
  Shifter #(.shift("lr")) shifter_2 (.in(A), .\dist (B[2:0]), .out(shifter_2_out));
  Comparator comparator_1 (.a(A), .b(B), .eq(comparator_1_eq));  // open: gt, lt
  xnor xnor_1 (xnor_1_out, A[7], B[7]);
  assign bit_extender_1_out = {{7{1'b0}}, comparator_1_eq};  // Bit_Extender bit_extender_1
  xor xor_2 (xor_2_out, A[7], N);
  and and_2 (V, xnor_1_out, xor_2_out);
  Multiplexer #(.select(4), .width(8)) multiplexer_1 (
    .in0(adder_1_out), .in1(subtractor_1_out), .in2(and_1_out), .in3(or_1_out), .in4(xor_1_out),
    .in5(not_1_out), .in6(shifter_1_out), .in7(shifter_2_out), .in8(bit_extender_1_out), .out({N, Y[6:0]}),
    .sel(OPCODE));  // open: in9, in10, in11, in12, in13, in14, in15
  nor nor_1 (Z, Y[0], Y[1], Y[2], Y[3], Y[4], Y[5], Y[6], N);

  assign Y[7] = N;
endmodule
